// Logisim project JogoOficialPedraPapelTesoura01.circ as structural Verilog: 2 circuits, main circuit main
module main (
  input  in_1,
  input  in_2,
  input  in_3
);

  wire _001, _01, _002, _02, _003, _03, _004, _04, AND1_out, AND2_out, AND3_out, AND4_out, AND5_out,
       AND6_out, AND7_out, AND8_out, AND9_out, and_1_out, and_2_out, and_3_out, and_4_out, and_5_out,
       and_6_out, and_7_out, and_8_out, and_11_out, and_13_out, and_14_out, and_15_out, and_16_out,
       and_17_out, and_18_out, and_19_out, botao, botao2, CLOCK_GERAL, CONFIRMAR_JOGADA, display2bs_1_a_2,
       display2bs_1_b_2, display2bs_1_c_2, display2bs_1_d_2, display2bs_1_e, display2bs_1_f, display2bs_1_g,
       display2bs_2_a_2, display2bs_2_b_2, display2bs_2_c_2, display2bs_2_d_2, display2bs_2_e,
       display2bs_2_f, display2bs_2_g, EMPATE, JOGADOR_1, JOGADOR_2, not_1_out, not_2_out, or_1_out,
       or_2_out, or_3_out, or_4_out, or_5_out, PAPEL01, PAPEL02, PEDRA01, PEDRA02, TESOURA01, TESOURA02,
       ZERAR_PLACAR;
  wire [3:0] PLACAR_J1, PLACAR_J2;
  wire [4:0] Contador_Papel_2_q, Contador_Papel_q, Contador_Pedra_2_q, Contador_Pedra_q, contador_q,
       Contador_Tesoura_q;
  wire [24:0] _1, _2, _3, _4, _5, _6, _7, _8, _9, _10, _11, _12, _13, _14, _15, A, A1, A2, A3, A4, A5, A6,
       A7, A8, A9, A10, A11, A12, A13, A14, A15, B, B1, B2, B3, B4, B5, B6, B7, B8, B9, B10, B11, B12, B13,
       B14, B15, C, C1, C2, C3, C4, C5, C6, C7, C8, C9, C10, C11, C12, C13, C14, C15, D, D1, D2, D3, D4, D5,
       D6, D7, D8, D9, D10, D11, D12, D13, D14, D15, E, F, G, H, I, J, K, L, M, N, O, rom_1_data, rom_2_data,
       rom_3_data, rom_4_data, rom_5_data, rom_6_data;

  Counter #(.width(5), .max('h1f), .trigger("falling")) Contador_Papel (
    .Q(Contador_Papel_q), .clk(and_2_out));  // open: load, D, count, carry, clr
  Counter #(.width(5), .max('h1f), .trigger("falling")) Contador_Pedra (
    .Q(Contador_Pedra_q), .clk(and_3_out));  // open: load, D, count, carry, clr
  Counter #(.width(5), .max('h1f), .trigger("falling")) Contador_Tesoura (
    .Q(Contador_Tesoura_q), .clk(and_1_out));  // open: load, D, count, carry, clr
  and and_1 (and_1_out, CLOCK_GERAL, TESOURA01);
  and and_2 (and_2_out, CLOCK_GERAL, PAPEL01);
  and and_3 (and_3_out, CLOCK_GERAL, PEDRA01);
  ROM #(.addrWidth(5), .dataWidth(25)) rom_1 (.addr(Contador_Papel_q), .data(rom_1_data));  // open: sel
  ROM #(.addrWidth(5), .dataWidth(25)) rom_2 (.addr(Contador_Pedra_q), .data(rom_2_data));  // open: sel
  ROM #(.addrWidth(5), .dataWidth(25)) rom_3 (.addr(Contador_Tesoura_q), .data(rom_3_data));  // open: sel
  Shift_Register #(.width(25), .length(15), .trigger("falling")) shift_register_1 (
    .in(rom_1_data), .clk(and_2_out), .q0(_1), .q1(_2), .q2(_3), .q3(_4), .q4(_5), .q5(_6), .q6(_7), .q7(_8),
    .q8(_9), .q9(_10), .q10(_11), .q11(_12), .q12(_13), .q13(_14), .q14(_15));  // open: shift, out, load, clr, d0, d1, d2, d3, d4, d5, d6, d7, d8, d9, d10, d11, d12, d13, d14
  Shift_Register #(.width(25), .length(15), .trigger("falling")) shift_register_2 (
    .in(rom_2_data), .clk(and_3_out), .q0(A1), .q1(A2), .q2(A3), .q3(A4), .q4(A5), .q5(A6), .q6(A7), .q7(A8),
    .q8(A9), .q9(A10), .q10(A11), .q11(A12), .q12(A13), .q13(A14), .q14(A15));  // open: shift, out, load, clr, d0, d1, d2, d3, d4, d5, d6, d7, d8, d9, d10, d11, d12, d13, d14
  Shift_Register #(.width(25), .length(15), .trigger("falling")) shift_register_3 (
    .in(rom_3_data), .clk(and_1_out), .q0(A), .q1(B), .q2(C), .q3(D), .q4(E), .q5(F), .q6(G), .q7(H), .q8(I),
    .q9(J), .q10(K), .q11(L), .q12(M), .q13(N), .q14(O));  // open: shift, out, load, clr, d0, d1, d2, d3, d4, d5, d6, d7, d8, d9, d10, d11, d12, d13, d14
  Clock clock_1 (.out(CLOCK_GERAL));
  Counter #(.width(4), .max('hf)) counter_1 (
    .Q(PLACAR_J1), .clk(JOGADOR_1), .clr(ZERAR_PLACAR));  // open: load, D, count, carry
  DotMatrix #(.matrixcols(15), .matrixrows(25)) dotmatrix_1 (
    .col0(A15), .col1(A14), .col2(A13), .col3(A12), .col4(A11), .col5(A10), .col6(A9), .col7(A8), .col8(A7),
    .col9(A6), .col10(A5), .col11(A4), .col12(A3), .col13(A2), .col14(A1));
  and and_4 (and_4_out, _01, or_1_out);
  and and_5 (and_5_out, _02, or_1_out);
  and and_6 (and_6_out, _03, or_1_out);
  or or_1 (or_1_out, in_3, not_1_out);
  not not_1 (not_1_out, in_1);
  DotMatrix #(.matrixcols(15), .matrixrows(25)) dotmatrix_2 (
    .col0(_15), .col1(_14), .col2(_13), .col3(_12), .col4(_11), .col5(_10), .col6(_9), .col7(_8), .col8(_7),
    .col9(_6), .col10(_5), .col11(_4), .col12(_3), .col13(_2), .col14(_1));
  and and_7 (and_7_out, _04, or_1_out);
  T_Flip_Flop #(.trigger("falling")) t_ff_1 (
    .clk(botao), .T(1'b1), .Q(_04), .reset(and_8_out));  // open: Qn, preset, en
  T_Flip_Flop #(.trigger("falling")) t_ff_2 (.clk(_04), .T(1'b1), .Q(_03), .reset(and_8_out));  // open: Qn, preset, en
  DotMatrix #(.matrixcols(15), .matrixrows(25)) dotmatrix_3 (
    .col0(O), .col1(N), .col2(M), .col3(L), .col4(K), .col5(J), .col6(I), .col7(H), .col8(G), .col9(F),
    .col10(E), .col11(D), .col12(C), .col13(B), .col14(A));
  display2bs display2bs_1 (
    .A(and_4_out), .B(and_5_out), .C(and_6_out), .D(and_7_out), .a_2(display2bs_1_a_2),
    .b_2(display2bs_1_b_2), .c_2(display2bs_1_c_2), .d_2(display2bs_1_d_2), .e(display2bs_1_e),
    .f(display2bs_1_f), .g(display2bs_1_g));
  T_Flip_Flop #(.trigger("falling")) t_ff_3 (.clk(_03), .T(1'b1), .Q(_02), .reset(and_8_out));  // open: Qn, preset, en
  _7_Segment_Display u_7_segment_display_1 (
    .g(display2bs_1_g), .f(display2bs_1_f), .a(display2bs_1_a_2), .b(display2bs_1_b_2), .e(display2bs_1_e),
    .d(display2bs_1_d_2), .c(display2bs_1_c_2));  // open: dp
  Button button_1 (.out(botao));
  Decoder #(.select(2)) decoder_1 (
    .out1(PEDRA01), .out2(PAPEL01), .out3(TESOURA01), .sel({_03, _04}));  // open: out0, en
  T_Flip_Flop #(.trigger("falling")) t_ff_4 (.clk(_02), .T(1'b1), .Q(_01), .reset(and_8_out));  // open: Qn, preset, en
  buf and_8 (and_8_out, _02);  // AND_Gate
  and and_9 (EMPATE, CONFIRMAR_JOGADA, or_2_out);
  and AND1 (AND1_out, PEDRA01, PEDRA02);
  Hex_Digit_Display hex_digit_display_1 (.value(PLACAR_J1));  // open: dp
  LED JOGADOR_1________________GANHOU (.in(JOGADOR_1));
  or or_2 (or_2_out, AND1_out, AND2_out, AND3_out);
  and AND2 (AND2_out, PAPEL01, PAPEL02);
  Button RESET (.out(ZERAR_PLACAR));
  Button button_2 (.out(CONFIRMAR_JOGADA));
  LED u_EMPATE (.in(EMPATE));
  and AND3 (AND3_out, TESOURA01, TESOURA02);
  and and_10 (JOGADOR_1, CONFIRMAR_JOGADA, or_3_out);
  T_Flip_Flop #(.trigger("falling")) t_ff_5 (
    .clk(botao2), .T(1'b1), .Q(_004), .reset(and_11_out));  // open: Qn, preset, en
  Hex_Digit_Display hex_digit_display_2 (.value(PLACAR_J2));  // open: dp
  and AND4 (AND4_out, PAPEL01, PEDRA02);
  T_Flip_Flop #(.trigger("falling")) t_ff_6 (
    .clk(_004), .T(1'b1), .Q(_003), .reset(and_11_out));  // open: Qn, preset, en
  LED JOGADOR_2_______________GANHOU (.in(JOGADOR_2));
  or or_3 (or_3_out, AND4_out, AND5_out, AND6_out);
  and AND5 (AND5_out, TESOURA01, PAPEL02);
  Decoder #(.select(2)) decoder_2 (
    .out1(PEDRA02), .out2(PAPEL02), .out3(TESOURA02), .sel({_003, _004}));  // open: out0, en
  T_Flip_Flop #(.trigger("falling")) t_ff_7 (
    .clk(_003), .T(1'b1), .Q(_002), .reset(and_11_out));  // open: Qn, preset, en
  DotMatrix #(.matrixcols(15), .matrixrows(25)) dotmatrix_4 (
    .col0(B15), .col1(B14), .col2(B13), .col3(B12), .col4(B11), .col5(B10), .col6(B9), .col7(B8), .col8(B7),
    .col9(B6), .col10(B5), .col11(B4), .col12(B3), .col13(B2), .col14(B1));
  and AND6 (AND6_out, PEDRA01, TESOURA02);
  T_Flip_Flop #(.trigger("falling")) t_ff_8 (
    .clk(_002), .T(1'b1), .Q(_001), .reset(and_11_out));  // open: Qn, preset, en
  buf and_11 (and_11_out, _002);  // AND_Gate
  display2bs display2bs_2 (
    .A(and_13_out), .B(and_14_out), .C(and_15_out), .D(and_16_out), .a_2(display2bs_2_a_2),
    .b_2(display2bs_2_b_2), .c_2(display2bs_2_c_2), .d_2(display2bs_2_d_2), .e(display2bs_2_e),
    .f(display2bs_2_f), .g(display2bs_2_g));
  and and_12 (JOGADOR_2, CONFIRMAR_JOGADA, or_4_out);
  and AND7 (AND7_out, PEDRA01, PAPEL02);
  Button button_3 (.out(botao2));
  or or_4 (or_4_out, AND7_out, AND8_out, AND9_out);
  and AND8 (AND8_out, PAPEL01, TESOURA02);
  DotMatrix #(.matrixcols(15), .matrixrows(25)) dotmatrix_5 (
    .col0(C15), .col1(C14), .col2(C13), .col3(C12), .col4(C11), .col5(C10), .col6(C9), .col7(C8), .col8(C7),
    .col9(C6), .col10(C5), .col11(C4), .col12(C3), .col13(C2), .col14(C1));
  _7_Segment_Display u_7_segment_display_2 (
    .g(display2bs_2_g), .f(display2bs_2_f), .a(display2bs_2_a_2), .b(display2bs_2_b_2), .e(display2bs_2_e),
    .d(display2bs_2_d_2), .c(display2bs_2_c_2));  // open: dp
  and AND9 (AND9_out, TESOURA01, PEDRA02);
  and and_13 (and_13_out, _001, or_5_out);
  and and_14 (and_14_out, _002, or_5_out);
  or or_5 (or_5_out, in_3, not_2_out);
  not not_2 (not_2_out, in_2);
  DotMatrix #(.matrixcols(15), .matrixrows(25)) dotmatrix_6 (
    .col0(D15), .col1(D13), .col2(D13), .col3(D12), .col4(D11), .col5(D10), .col6(D9), .col7(D8), .col8(D7),
    .col9(D6), .col10(D5), .col11(D4), .col12(D3), .col13(D2), .col14(D1));
  and and_15 (and_15_out, _003, or_5_out);
  and and_16 (and_16_out, _004, or_5_out);
  Counter #(.width(4), .max('hf)) counter_2 (
    .Q(PLACAR_J2), .clk(JOGADOR_2), .clr(ZERAR_PLACAR));  // open: load, D, count, carry
  and and_17 (and_17_out, CLOCK_GERAL, TESOURA02);
  Counter #(.width(5), .max('h1f), .trigger("falling")) Contador_Pedra_2 (
    .Q(Contador_Pedra_2_q), .clk(and_19_out));  // open: load, D, count, carry, clr
  Counter #(.width(5), .max('h1f), .trigger("falling")) contador (
    .Q(contador_q), .clk(and_17_out));  // open: load, D, count, carry, clr
  Counter #(.width(5), .max('h1f), .trigger("falling")) Contador_Papel_2 (
    .Q(Contador_Papel_2_q), .clk(and_18_out));  // open: load, D, count, carry, clr
  and and_18 (and_18_out, CLOCK_GERAL, PAPEL02);
  ROM #(.addrWidth(5), .dataWidth(25)) rom_4 (.addr(Contador_Pedra_2_q), .data(rom_4_data));  // open: sel
  and and_19 (and_19_out, CLOCK_GERAL, PEDRA02);
  ROM #(.addrWidth(5), .dataWidth(25)) rom_5 (.addr(contador_q), .data(rom_5_data));  // open: sel
  ROM #(.addrWidth(5), .dataWidth(25)) rom_6 (.addr(Contador_Papel_2_q), .data(rom_6_data));  // open: sel
  Shift_Register #(.width(25), .length(15), .trigger("falling")) shift_register_4 (
    .in(rom_4_data), .clk(and_19_out), .q0(B1), .q1(B2), .q2(B3), .q3(B4), .q4(B5), .q5(B6), .q6(B7),
    .q7(B8), .q8(B9), .q9(B10), .q10(B11), .q11(B12), .q12(B13), .q13(B14), .q14(B15));  // open: shift, out, load, clr, d0, d1, d2, d3, d4, d5, d6, d7, d8, d9, d10, d11, d12, d13, d14
  Shift_Register #(.width(25), .length(15), .trigger("falling")) shift_register_5 (
    .in(rom_5_data), .clk(and_17_out), .q0(D1), .q1(D2), .q2(D3), .q3(D4), .q4(D5), .q5(D6), .q6(D7),
    .q7(D8), .q8(D9), .q9(D10), .q10(D11), .q11(D12), .q12(D13), .q13(D14), .q14(D15));  // open: shift, out, load, clr, d0, d1, d2, d3, d4, d5, d6, d7, d8, d9, d10, d11, d12, d13, d14
  Shift_Register #(.width(25), .length(15), .trigger("falling")) shift_register_6 (
    .in(rom_6_data), .clk(and_18_out), .q0(C1), .q1(C2), .q2(C3), .q3(C4), .q4(C5), .q5(C6), .q6(C7),
    .q7(C8), .q8(C9), .q9(C10), .q10(C11), .q11(C12), .q12(C13), .q13(C14), .q14(C15));  // open: shift, out, load, clr, d0, d1, d2, d3, d4, d5, d6, d7, d8, d9, d10, d11, d12, d13, d14

  // Other names for the same wires on the sheet: Pronto_1 = in_1; Pronto_2 = in_2; REVELAR = in_3

  // Notes on the sheet:
  //   contents of rom_1 (hex, n*v repeats v):
  //   7ffffc 400004 401204 401204 201204 100004 ffffc
  //   contents of rom_2 (hex, n*v repeats v):
  //   7ffe0 7ffff0 fffff8 fffff8 7ffff0 7ffe0
  //   contents of rom_3 (hex, n*v repeats v):
  //   7c003e 183c041 1803c41 7e03fe 1ff80 7e03fe 1803c41 183c041 7c003e
  //   PEDRA
  //   q0
  //   PAPEL
  //   q01
  //   q02
  //   TESOURA
  //   q03
  //   q0
  //   q01
  //   q02
  //   q03
  //   PEDRA
  //   PAPEL
  //   TESOURA
  //   contents of rom_4 (hex, n*v repeats v):
  //   7ffe0 7ffff0 fffff8 fffff8 7ffff0 7ffe0
  //   contents of rom_5 (hex, n*v repeats v):
  //   7c003e 183c041 1803c41 7e03fe 1ff80 7e03fe 1803c41 183c041 7c003e
  //   contents of rom_6 (hex, n*v repeats v):
  //   7ffffc 400004 401204 401204 201204 100004 ffffc
endmodule

module display2bs (
  input  A,
  input  B,
  input  C,
  input  D,
  output a_2,
  output b_2,
  output c_2,
  output d_2,
  output e,
  output f,
  output g
);

  wire and_1_out, and_2_out, and_3_out, and_4_out, and_5_out, and_6_out, and_7_out, and_8_out, and_9_out,
       and_10_out, not_1_out, not_2_out, not_3_out, not_4_out, xnor_1_out, xnor_2_out, xor_1_out;

  not not_1 (not_1_out, A);
  not not_2 (not_2_out, B);
  not not_3 (not_3_out, C);
  not not_4 (not_4_out, D);
  and and_1 (and_1_out, not_2_out, not_4_out);
  and and_2 (and_2_out, not_2_out, C);
  and and_3 (and_3_out, C, not_4_out);
  and and_4 (and_4_out, B, not_3_out, D);
  and and_5 (and_5_out, not_2_out, not_4_out);
  and and_6 (and_6_out, C, not_4_out);
  and and_7 (and_7_out, not_3_out, not_4_out);
  and and_8 (and_8_out, B, not_3_out);
  and and_9 (and_9_out, B, not_4_out);
  and and_10 (and_10_out, C, not_4_out);
  xnor xnor_1 (xnor_1_out, B, D);
  xnor xnor_2 (xnor_2_out, C, D);
  xor xor_1 (xor_1_out, B, C);
  or or_1 (a_2, xnor_1_out, A, C);
  or or_2 (b_2, xnor_2_out, not_2_out);
  or or_3 (c_2, B, not_3_out, D);
  or or_4 (d_2, A, and_1_out, and_2_out, and_3_out, and_4_out);
  or or_5 (e, and_5_out, and_6_out);
  or or_6 (f, A, and_7_out, and_8_out, and_9_out);
  or or_7 (g, A, xor_1_out, and_10_out);
endmodule
